// Logisim project A_Garcia_Lopez_Andres.circ as structural Verilog: 3 circuits, main circuit Circ-1
module Circ_1 (
  input  A,
  input  B,
  input  C,
  input  D,
  output F
);

  wire nor_1_out, nor_2_out, nor_3_out, not_1_out, not_2_out, not_3_out;

  not not_1 (not_1_out, A);
  not not_2 (not_2_out, B);
  not not_3 (not_3_out, C);
  nor nor_1 (nor_1_out, B, C, D);
  nor nor_2 (nor_2_out, not_1_out, C);
  nor nor_3 (nor_3_out, not_2_out, not_3_out);
  nor nor_4 (F, nor_1_out, nor_2_out, nor_3_out);
endmodule

module Circ_2 (
  input  D,
  input  C,
  input  A,
  input  B,
  output F
);

  wire not_1_out, or_1_out;

  or or_1 (or_1_out, D, C);
  not not_1 (not_1_out, C);
  Multiplexer #(.select(2)) multiplexer_1 (
    .in0(or_1_out), .in1(not_1_out), .in2(C), .in3(1'b0), .out(F), .sel({A, B}), .en(1'b1));
endmodule

module Circ_3 (
  input  E
);

  wire and_1_out, and_2_out, Clear_out, clock_1_out, demultiplexer_1_out4, demultiplexer_1_out5,
       demultiplexer_1_out6, not_1_out, not_2_out, or_1_out, or_2_out, Preset_out;
  wire [1:0] t_ff_2_q;

  Clock clock_1 (.out(clock_1_out));
  Button Preset (.out(Preset_out));
  Button Clear (.out(Clear_out));
  or or_1 (or_1_out, and_1_out, and_2_out);
  and and_1 (and_1_out, not_1_out, t_ff_2_q[1], t_ff_2_q[0]);
  not not_1 (not_1_out, E);
  and and_2 (and_2_out, E, not_2_out, t_ff_2_q[0]);
  not not_2 (not_2_out, t_ff_2_q[1]);
  T_Flip_Flop t_ff_1 (
    .clk(clock_1_out), .T(or_1_out), .Q(t_ff_2_q[1]), .preset(Preset_out), .reset(Clear_out), .en(1'b1));  // open: Qn
  Demultiplexer #(.select(3)) demultiplexer_1 (
    .out4(demultiplexer_1_out4), .out5(demultiplexer_1_out5), .out6(demultiplexer_1_out6),
    .sel({E, t_ff_2_q}), .en(1'b1));  // open: out0, out1, out2, out3, out7, in
  or or_2 (or_2_out, demultiplexer_1_out4, demultiplexer_1_out5, demultiplexer_1_out6);
  T_Flip_Flop t_ff_2 (
    .clk(clock_1_out), .T(or_2_out), .Q(t_ff_2_q[0]), .preset(Preset_out), .reset(Clear_out), .en(1'b1));  // open: Qn
endmodule
