// Logisim project A_garcia_andres.circ as structural Verilog
module main (
);


  // Notes on the sheet:
  //   Fill the following data;
  //   Find: 
  //   Fill the following data;
  //   Part 1. Assigned positions for F = 0,1,2,4,7
  //   ID (or DNI) = 71367735T
  //   Part 2. Assigned positions for G = 0,4,6,7,11,13,14
  //   Desing of the main circuit below
  //    COMPUTER TECHNOLOGY  EXAM 1
  //   SOP,       F(A,B,C)= (A`B`C`)+(A`B`C)+(A`BC`)+(AB`C`)+(ABC)
  //   POS        F(A,B,C)= (A+B+C)(A+B+C`)(A+B`+C)(A`+B+C)(A`+B`+C`)
  //   ------------------------------------------------------------------------------------------------------------------------------------------
  //   ------------------------------------------------------------------------------------------------------------------------------------------
endmodule

module Subcircuit_1_1 (
  input  A,
  input  B,
  input  C,
  output F
);

  wire nor_1_out, nor_2_out, nor_3_out, not_1_out, not_2_out, not_3_out;

  not not_1 (not_1_out, A);
  not not_2 (not_2_out, B);
  not not_3 (not_3_out, C);
  nor nor_1 (nor_1_out, not_1_out, B, not_3_out);
  nor nor_2 (nor_2_out, not_1_out, not_2_out, not_3_out);
  nor nor_3 (nor_3_out, not_1_out, not_2_out, C);
  nor nor_4 (F, nor_1_out, nor_2_out, nor_3_out);
endmodule

module Subcircuit_1_2 (
  input  A,
  input  C,
  input  B,
  output F
);

  wire and_1_out, decoder_1_out0, decoder_1_out1, decoder_1_out2, decoder_2_out0, decoder_2_out3, not_1_out,
       not_2_out, not_3_out, not_4_out, not_5_out, not_6_out;

  Decoder #(.select(2), .disabled(0)) decoder_1 (
    .out0(decoder_1_out0), .out1(decoder_1_out1), .out2(decoder_1_out2), .sel({B, C}), .en(not_1_out));  // open: out3
  not not_1 (not_1_out, A);
  Decoder #(.select(2), .disabled(0)) decoder_2 (
    .out0(decoder_2_out0), .out3(decoder_2_out3), .sel({B, C}), .en(A));  // open: out1, out2
  not not_2 (not_2_out, decoder_1_out0);
  not not_3 (not_3_out, decoder_1_out1);
  not not_4 (not_4_out, decoder_1_out2);
  not not_5 (not_5_out, decoder_2_out0);
  not not_6 (not_6_out, decoder_2_out3);
  not not_7 (F, and_1_out);
  and and_1 (and_1_out, not_2_out, not_3_out, not_4_out, not_5_out, not_6_out);
endmodule

module Subcircuit_2_2 (
  input  D,
  input  C,
  input  B,
  input  A,
  output G
);

  wire not_1_out;

  not not_1 (not_1_out, D);
  Multiplexer #(.select(3)) multiplexer_1 (
    .in0(not_1_out), .in1(1'b0), .in2(not_1_out), .in3(1'b1), .in4(1'b0), .in5(D), .in6(D), .in7(not_1_out),
    .out(G), .sel({A, B, C}));  // open: en
endmodule
