// Logisim project casa.circ as structural Verilog: 5 circuits, main circuit main
module main (
);


  // Notes on the sheet:
  //   Fill the following data;
  //   Find: 
  //   Fill the following data;
  //   Part 1. Assigned positions for F = 0,1,2,4,7
  //   ID (or DNI) = 71367735T
  //   POS        F(A,B,C)= (A+B'+C').(A'+B+C').(A'+B'+C)
  //   Part 2. Assigned positions for G = 0,4,6,7,11,13,14
  //   Desing of the main circuit below
  //    COMPUTER TECHNOLOGY  EXAM 1
  //   ------------------------------------------------------------------------------------------------------------------------------------------
  //   ------------------------------------------------------------------------------------------------------------------------------------------
  //   SOP,       F(A,B,C)= (A`B`C`)+(A`B`C)+(A`BC`)+(AB`C`)+(ABC) -> (A'B')+(B'C')+(A'C')+(ABC)
endmodule

module Subcircuit_1_1 (
  input  A,
  input  B,
  input  C,
  output F
);

  wire nor_1_out, nor_2_out, nor_3_out, not_1_out, not_2_out, not_3_out;

  not not_1 (not_1_out, A);
  not not_2 (not_2_out, B);
  not not_3 (not_3_out, C);
  nor nor_1 (nor_1_out, A, not_2_out, not_3_out);
  nor nor_2 (nor_2_out, not_1_out, B, not_3_out);
  nor nor_3 (nor_3_out, not_1_out, not_2_out, C);
  nor nor_4 (F, nor_1_out, nor_2_out, nor_3_out);
endmodule

module Subcircuit_1_2 (
  input  E,
  input  A,
  input  C,
  input  B,
  output out_5,
  output out_6,
  output out_7,
  output out_8,
  output out_9,
  output out_10,
  output out_11,
  output out_12
);

  wire decoder_1_out0, decoder_1_out1, decoder_2_out0, decoder_2_out1, decoder_2_out2, decoder_2_out3,
       decoder_3_out0, decoder_3_out1, decoder_3_out2, decoder_3_out3;

  Decoder #(.select(2), .disabled(0)) decoder_1 (
    .out0(decoder_1_out0), .out1(decoder_1_out1), .sel({A, 1'b0}), .en(E));  // open: out2, out3
  Decoder #(.select(2), .disabled(0)) decoder_2 (
    .out0(decoder_2_out0), .out1(decoder_2_out1), .out2(decoder_2_out2), .out3(decoder_2_out3), .sel({B, C}),
    .en(decoder_1_out0));
  Decoder #(.select(2), .disabled(0)) decoder_3 (
    .out0(decoder_3_out0), .out1(decoder_3_out1), .out2(decoder_3_out2), .out3(decoder_3_out3), .sel({B, C}),
    .en(decoder_1_out1));
  not not_1 (out_5, decoder_2_out0);
  not not_2 (out_6, decoder_2_out1);
  not not_3 (out_7, decoder_2_out2);
  not not_4 (out_8, decoder_2_out3);
  not not_5 (out_9, decoder_3_out0);
  not not_6 (out_10, decoder_3_out1);
  not not_7 (out_11, decoder_3_out2);
  not not_8 (out_12, decoder_3_out3);
endmodule

module Subcircuit_2_1 (
  input  A,
  input  B,
  input  C,
  input  D,
  output out_5
);

  wire not_1_out, subcircuit_1_2_1_out_5, subcircuit_1_2_1_out_9, subcircuit_1_2_1_out_11,
       subcircuit_1_2_1_out_12, subcircuit_1_2_2_out_8, subcircuit_1_2_2_out_10, subcircuit_1_2_2_out_11;

  not not_1 (not_1_out, A);
  Subcircuit_1_2 subcircuit_1_2_1 (
    .E(not_1_out), .A(B), .C(C), .B(D), .out_5(subcircuit_1_2_1_out_5), .out_9(subcircuit_1_2_1_out_9),
    .out_11(subcircuit_1_2_1_out_11), .out_12(subcircuit_1_2_1_out_12));  // open: out_6, out_7, out_8, out_10
  Subcircuit_1_2 subcircuit_1_2_2 (
    .E(A), .A(B), .C(C), .B(D), .out_8(subcircuit_1_2_2_out_8), .out_10(subcircuit_1_2_2_out_10),
    .out_11(subcircuit_1_2_2_out_11));  // open: out_5, out_6, out_7, out_9, out_12
  nand nand_1 (out_5, subcircuit_1_2_1_out_5, subcircuit_1_2_1_out_9, subcircuit_1_2_1_out_11, subcircuit_1_2_1_out_12, subcircuit_1_2_2_out_8, subcircuit_1_2_2_out_10, subcircuit_1_2_2_out_11);
endmodule

module Subcircuit_2_2 (
  input  D,
  input  C,
  input  B,
  input  A,
  output G
);

  wire not_1_out;

  not not_1 (not_1_out, D);
  Multiplexer #(.select(3)) multiplexer_1 (
    .in0(not_1_out), .in1(1'b0), .in2(not_1_out), .in3(1'b1), .in4(1'b0), .in5(D), .in6(D), .in7(not_1_out),
    .out(G), .sel({A, B, C}));  // open: en
endmodule
