// Logisim project A_Garcia_Andres.circ as structural Verilog: 1 circuit, main circuit main
module main (
);

  wire and_1_out, and_2_out, and_3_out, and_4_out, and_5_out, Clock_out, d_ff_1_q, d_ff_2_q, d_ff_3_q,
       d_ff_4_q, not_1_out, not_2_out, not_3_out, not_4_out, not_5_out, not_6_out, not_7_out, or_1_out,
       or_2_out, or_3_out;

  Clock Clock (.out(Clock_out));
  D_Flip_Flop d_ff_1 (.clk(Clock_out), .D(d_ff_4_q), .Q(d_ff_1_q));  // open: Qn, preset, en, reset
  or or_1 (or_1_out, and_1_out, not_1_out, not_2_out);
  not not_1 (not_1_out, d_ff_3_q);
  not not_2 (not_2_out, d_ff_2_q);
  and and_1 (and_1_out, not_3_out, d_ff_4_q);
  not not_3 (not_3_out, d_ff_1_q);
  D_Flip_Flop d_ff_2 (.clk(Clock_out), .D(or_1_out), .Q(d_ff_2_q));  // open: Qn, preset, en, reset
  and and_2 (and_2_out, d_ff_4_q, not_5_out);
  D_Flip_Flop d_ff_3 (.clk(Clock_out), .D(or_2_out), .Q(d_ff_3_q));  // open: Qn, preset, en, reset
  or or_2 (or_2_out, and_2_out, and_3_out);
  and and_3 (and_3_out, not_4_out, d_ff_2_q);
  not not_4 (not_4_out, d_ff_1_q);
  not not_5 (not_5_out, d_ff_3_q);
  D_Flip_Flop d_ff_4 (.clk(Clock_out), .D(or_3_out), .Q(d_ff_4_q));  // open: Qn, preset, en, reset
  or or_3 (or_3_out, and_4_out, and_5_out);
  and and_4 (and_4_out, not_7_out, d_ff_4_q);
  and and_5 (and_5_out, not_6_out, d_ff_3_q);
  not not_6 (not_6_out, d_ff_1_q);
  not not_7 (not_7_out, d_ff_2_q);

  // Notes on the sheet:
  //   ID Number: 71367735T
  //   Sequence Assigned: 0 4 6 7 11 13 14
  //   D3
  //   D2
  //   D3=Q0
  //   D2=Q2'+Q1'+Q3'Q0'
  //   D1
  //   D0
  //   D1=Q1'Q0+Q3'Q2
  //   D0=Q2'Q0+Q3'Q1
endmodule
