// Logisim project Prueba.circ as structural Verilog: 2 circuits, main circuit main
module main (
  output Q3,
  output Q2,
  output Q1,
  output Q0
);

  wire and_1_out, and_2_out, and_3_out, and_4_out, and_5_out, Clear_out, Clock_out, d_ff_1_qn, d_ff_2_qn,
       d_ff_3_qn, d_ff_4_qn, or_1_out, or_2_out, or_3_out, Preset_out;
  wire [2:0] counter_1_counter;

  Button Preset (.out(Preset_out));
  Button Clear (.out(Clear_out));
  Clock Clock (.out(Clock_out));
  D_Flip_Flop d_ff_1 (
    .clk(Clock_out), .D(Q0), .Q(Q3), .Qn(d_ff_1_qn), .preset(Preset_out), .en(1'b1), .reset(Clear_out));
  and and_1 (and_1_out, d_ff_4_qn, d_ff_1_qn);
  D_Flip_Flop d_ff_2 (
    .clk(Clock_out), .D(or_1_out), .Q(Q2), .Qn(d_ff_2_qn), .preset(Preset_out), .en(1'b1), .reset(Clear_out));
  or or_1 (or_1_out, and_1_out, d_ff_3_qn, d_ff_2_qn);
  and and_2 (and_2_out, Q2, d_ff_1_qn);
  and and_3 (and_3_out, d_ff_3_qn, Q0);
  D_Flip_Flop d_ff_3 (
    .clk(Clock_out), .D(or_2_out), .Q(Q1), .Qn(d_ff_3_qn), .preset(Preset_out), .en(1'b1), .reset(Clear_out));
  or or_2 (or_2_out, and_3_out, and_2_out);
  and and_4 (and_4_out, Q1, d_ff_1_qn);
  and and_5 (and_5_out, Q0, d_ff_2_qn);
  or or_3 (or_3_out, and_5_out, and_4_out);
  D_Flip_Flop d_ff_4 (
    .clk(Clock_out), .D(or_3_out), .Q(Q0), .Qn(d_ff_4_qn), .preset(Preset_out), .en(1'b1), .reset(Clear_out));
  Counter counter_1 (.Clock_Signal(Clock_out), .Preset(Preset_out), .Clear(Clear_out), .Counter(counter_1_counter));
  Hex_Digit_Display hex_digit_display_1 (.value({Q3, Q2, Q1, Q0}));  // open: dp
  Hex_Digit_Display hex_digit_display_2 (.value({1'b0, counter_1_counter}));  // open: dp

  // Notes on the sheet:
  //   0 - 4 - 6 - 7 - 11 - 13 - 14
  //   D3 = Q0
  //   D2 = Q2`+ Q1`+ Q3`Q0`
  //   D1 = Q3`Q2 + Q1`Q0
  //   D0 = Q3`Q2 + Q1Q0
endmodule

module Counter (
  input  Clock_Signal,
  input  Preset,
  input  Clear,
  output [2:0] Counter
);

  wire and_1_out, and_2_out, d_ff_2_qn, or_1_out, xor_1_out;

  and and_1 (and_1_out, Counter[1], Counter[0]);
  T_Flip_Flop t_ff_1 (
    .clk(Clock_Signal), .T(and_1_out), .Q(Counter[2]), .preset(Preset), .reset(Clear), .en(1'b1));  // open: Qn
  xor xor_1 (xor_1_out, Counter[0], Counter[1]);
  D_Flip_Flop d_ff_1 (
    .clk(Clock_Signal), .D(xor_1_out), .Q(Counter[1]), .preset(Preset), .en(1'b1), .reset(Clear));  // open: Qn
  and and_2 (and_2_out, Counter[2], Counter[1]);
  or or_1 (or_1_out, and_2_out, d_ff_2_qn);
  D_Flip_Flop d_ff_2 (
    .clk(Clock_Signal), .D(or_1_out), .Q(Counter[0]), .Qn(d_ff_2_qn), .preset(Clear), .en(1'b1));  // open: reset
endmodule
