// Logisim project Exercise2.circ as structural Verilog: 1 circuit, main circuit main
module main (
  input  A,
  input  B,
  input  C,
  output F
);

  wire and_1_out, and_2_out, not_1_out, not_2_out, not_3_out, or_1_out;

  not not_1 (not_1_out, B);
  not not_2 (not_2_out, C);
  not not_3 (not_3_out, A);
  or or_1 (or_1_out, not_1_out, not_2_out);
  and and_1 (and_1_out, not_3_out, or_1_out);
  and and_2 (and_2_out, A, C);
  or or_2 (F, and_1_out, and_2_out);
endmodule
