// Logisim project Exercise3.circ as structural Verilog: 1 circuit, main circuit main
module main (
  input  A,
  input  B,
  input  C,
  output F
);

  wire not_1_out, not_2_out, not_3_out, or_1_out, or_2_out;

  not not_1 (not_1_out, A);
  not not_2 (not_2_out, B);
  not not_3 (not_3_out, C);
  or or_1 (or_1_out, not_1_out, C);
  or or_2 (or_2_out, A, not_2_out, not_3_out);
  and and_1 (F, or_1_out, or_2_out);
endmodule
