// Logisim project Introduction.circ as structural Verilog: 1 circuit, main circuit main
module main (
  input  A,
  input  B,
  input  C,
  output F
);

  wire _1_out, and_1_out, not_1_out;

  not not_1 (not_1_out, C);
  and _1 (_1_out, A, B);
  and and_1 (and_1_out, not_1_out, B);
  or or_1 (F, _1_out, and_1_out);
endmodule
