// Logisim project Part1.circ as structural Verilog: 1 circuit, main circuit main
module main (
  input  [2:0] in_1,
  input  A,
  input  B,
  input  C,
  input  D,
  input  [1:0] in_6,
  output _0,
  output _1,
  output _2,
  output _3,
  output _5,
  output _4,
  output _6,
  output _7,
  output out_15
);

  Decoder #(.select(3)) decoder_1 (
    .out0(_0), .out1(_1), .out2(_2), .out3(_3), .out4(_4), .out5(_5), .out6(_6), .out7(_7), .sel(in_1),
    .en(1'b1));
  Multiplexer #(.select(2)) multiplexer_1 (.in0(A), .in1(B), .in2(C), .in3(D), .out(out_15), .sel(in_6), .en(1'b1));
endmodule
