// Logisim project Part2.circ as structural Verilog: 1 circuit, main circuit main
module main (
  input  [2:0] in_1,
  input  in_2,
  input  in_3,
  input  [2:0] in_4,
  output _1,
  output _1_2
);

  wire decoder_1_out2, decoder_1_out5, decoder_1_out6;

  Decoder #(.select(3)) decoder_1 (
    .out2(decoder_1_out2), .out5(decoder_1_out5), .out6(decoder_1_out6), .sel(in_1), .en(1'b1));  // open: out0, out1, out3, out4, out7
  Multiplexer #(.select(3)) multiplexer_1 (
    .in0(in_2), .in1(in_2), .in2(in_3), .in3(in_2), .in4(in_2), .in5(in_3), .in6(in_3), .in7(in_2),
    .out(_1_2), .sel(in_4), .en(1'b1));
  or or_1 (_1, decoder_1_out2, decoder_1_out5, decoder_1_out6);

  // Notes on the sheet:
  //   F(A,B,C)=A!BC+B!C
endmodule
