// Logisim project Part3.circ as structural Verilog: 2 circuits, main circuit main
module main (
  input  Enable,
  input  N1,
  input  N0,
  output S4,
  output S3,
  output S2,
  output S1,
  output S0
);

  dec2x4 dec2x4_1 (.N1(N1), .N0(N0), .Enable(Enable), .S4(S4), .S3(S3), .S2(S2), .S1(S1), .S0(S0));
endmodule

module dec2x4 (
  input  Enable,
  input  N1,
  input  N0,
  output S4,
  output S3,
  output S2,
  output S1,
  output S0
);

  wire and_4_out, not_1_out, not_2_out, not_3_out, not_4_out;

  not not_1 (not_1_out, N0);
  not not_2 (not_2_out, N1);
  not not_3 (not_3_out, N0);
  not not_4 (not_4_out, N0);
  and and_1 (S4, Enable, N1, N0);
  and and_2 (S3, Enable, not_1_out, N1);
  and and_3 (S2, Enable, not_2_out);
  and and_4 (and_4_out, Enable, not_3_out, N1);
  and and_5 (S0, Enable, not_4_out);
  or or_1 (S1, S2, and_4_out);
endmodule
