// Logisim project 3.circ as structural Verilog: 4 circuits, main circuit main
module main (
  input  [7:0] in_1,
  output F,
  output NO_INPUTS_1,
  output G
);

  wire circuit1_1_any_1;
  wire [3:0] circuit1_1_bcd, controlled_buffer_1_out;

  Circuit1 circuit1_1 (
    .in_1(in_1), .NO_INPUTS_1(NO_INPUTS_1), .ANY_1(circuit1_1_any_1), .BCD(circuit1_1_bcd));  // open: PRI_INPUT
  assign controlled_buffer_1_out = circuit1_1_any_1 ? circuit1_1_bcd : 4'bz;  // Controlled_Buffer controlled_buffer_1
  Hex_Digit_Display hex_digit_display_1 (.value(controlled_buffer_1_out));  // open: dp
  Circuit2 circuit2_1 (
    .A(controlled_buffer_1_out[2]), .B(controlled_buffer_1_out[1]), .C(controlled_buffer_1_out[0]), .F(F));
  Circuit3 circuit3_1 (
    .A(controlled_buffer_1_out[2]), .B(controlled_buffer_1_out[1]), .C(controlled_buffer_1_out[0]), .G(G));

  // Notes on the sheet:
  //   INPUT
  //   7 1 3 6 7 7 3 5
  //   Circuit 1
  //   NUMBER OF PRIOR BIT
  //   Circuit 2
  //   Circuit 3
endmodule

module Circuit1 (
  input  [7:0] in_1,
  output NO_INPUTS_1,
  output [2:0] PRI_INPUT,
  output ANY_1,
  output [3:0] BCD
);

  Priority_Encoder priority_encoder_1 (
    .in0(in_1[0]), .in1(in_1[1]), .in2(in_1[2]), .in3(in_1[3]), .in4(in_1[4]), .in5(in_1[5]), .in6(in_1[6]),
    .in7(in_1[7]), .out(BCD[2:0]), .en_in(1'b1), .gs(ANY_1), .en_out(NO_INPUTS_1));

  assign BCD[3] = 1'b0;
  assign PRI_INPUT = BCD[2:0];
endmodule

module Circuit2 (
  input  A,
  input  B,
  input  C,
  output F
);

  wire not_1_out;

  not not_1 (not_1_out, C);
  Multiplexer #(.select(2)) multiplexer_1 (
    .in0(1'b0), .in1(not_1_out), .in2(not_1_out), .in3(not_1_out), .out(F), .sel({B, A}), .en(1'b1));
endmodule

module Circuit3 (
  input  A,
  input  B,
  input  C,
  output G
);

  wire not_1_out;

  not not_1 (not_1_out, C);
  Multiplexer #(.select(2)) multiplexer_1 (
    .in0(C), .in1(not_1_out), .in2(not_1_out), .in3(C), .out(G), .sel({B, A}), .en(1'b1));
endmodule
