// Logisim project sol_pr3_1A.circ as structural Verilog: 4 circuits, main circuit main
module main (
  input  [7:0] _7_6_5_4_3_2_1_0,
  output F,
  output G
);

  wire circuit1_1_no_active_bits, not_1_out;
  wire [3:0] circuit1_1_n_bcd, controlled_buffer_1_out;

  Circuit1 circuit1_1 (
    ._7_6_5_4_3_2_1_0(_7_6_5_4_3_2_1_0), .N_BCD(circuit1_1_n_bcd), .No_active_bits(circuit1_1_no_active_bits));  // open: NO_INPUTS_1, N
  LED No_active_bits (.in(not_1_out));
  not not_1 (not_1_out, circuit1_1_no_active_bits);
  Hex_Digit_Display hex_digit_display_1 (.value(controlled_buffer_1_out));  // open: dp
  assign controlled_buffer_1_out = circuit1_1_no_active_bits ? circuit1_1_n_bcd : 4'bz;  // Controlled_Buffer controlled_buffer_1
  Circuit2 circuit2_1 (
    .A(controlled_buffer_1_out[2]), .B(controlled_buffer_1_out[1]), .C(controlled_buffer_1_out[0]), .F(F));
  LED led_1 (.in(F));
  Circuit3 circuit3_1 (
    .B(controlled_buffer_1_out[1]), .C(controlled_buffer_1_out[0]), .A(controlled_buffer_1_out[2]), .G(G));
  LED led_2 (.in(G));

  // Notes on the sheet:
  //   INPUT
  //   CIRCUIT 1
  //   NUMBER OF PRIOR INPUT
  //   CIRCUIT 2
  //   A B C
  //   B
  //   C
  //   EVEN NUMBER
  //   CIRCUIT 3
  //   A
  //   ODD NUMBER OF 1's
endmodule

module Circuit1 (
  input  [7:0] _7_6_5_4_3_2_1_0,
  output NO_INPUTS_1,
  output [2:0] N,
  output No_active_bits,
  output [3:0] N_BCD
);

  Priority_Encoder priority_encoder_1 (
    .in0(_7_6_5_4_3_2_1_0[0]), .in1(_7_6_5_4_3_2_1_0[1]), .in2(_7_6_5_4_3_2_1_0[2]),
    .in3(_7_6_5_4_3_2_1_0[3]), .in4(_7_6_5_4_3_2_1_0[4]), .in5(_7_6_5_4_3_2_1_0[5]),
    .in6(_7_6_5_4_3_2_1_0[6]), .in7(_7_6_5_4_3_2_1_0[7]), .out(N), .en_in(1'b1), .gs(No_active_bits),
    .en_out(NO_INPUTS_1));

  assign N_BCD = {1'b0, N};

  // Notes on the sheet:
  //   ANY INPUTS IS 1
  //   NUMBER OF PRIOR INPUT
  //   BCD ACTIVE PRIOR INPUT
endmodule

module Circuit2 (
  input  A,
  input  B,
  input  C,
  output F
);

  wire not_1_out;

  not not_1 (not_1_out, C);
  Multiplexer #(.select(2)) multiplexer_1 (
    .in0(1'b0), .in1(not_1_out), .in2(not_1_out), .in3(not_1_out), .out(F), .sel({B, A}), .en(1'b1));
  LED led_1 (.in(F));

  // Notes on the sheet:
  //   NUMERO PAR
endmodule

module Circuit3 (
  input  A,
  input  B,
  input  C,
  output G
);

  wire multiplexer_1_out, multiplexer_2_out, not_1_out;

  not not_1 (not_1_out, A);
  Multiplexer #(.select(2), .disabled(0)) multiplexer_1 (
    .in0(1'b0), .in1(1'b1), .in2(1'b1), .in3(1'b0), .out(multiplexer_1_out), .sel({B, C}), .en(not_1_out));
  Multiplexer #(.select(2), .disabled(0)) multiplexer_2 (
    .in0(1'b1), .in1(1'b0), .in2(1'b0), .in3(1'b1), .out(multiplexer_2_out), .sel({B, C}), .en(A));
  or or_1 (G, multiplexer_1_out, multiplexer_2_out);
  LED led_1 (.in(G));

  // Notes on the sheet:
  //   ODD NUMBER OF 1's
endmodule
