// Logisim project Part1.circ as structural Verilog: 1 circuit, main circuit main
module main (
  input  in_1,
  input  in_2,
  input  in_3,
  output out_4,
  output out_5
);

  wire button_1_out, button_2_out, button_3_out, button_4_out, button_5_out, button_6_out;

  Button button_1 (.out(button_1_out));
  D_Flip_Flop d_ff_1 (
    .clk(button_1_out), .D(in_2), .Q(out_4), .preset(button_3_out), .en(1'b1), .reset(button_2_out));  // open: Qn
  Button button_2 (.out(button_2_out));
  Button button_3 (.out(button_3_out));
  Button button_4 (.out(button_4_out));
  Button button_5 (.out(button_5_out));
  J_K_Flip_Flop j_k_ff_1 (
    .J(in_1), .clk(button_4_out), .K(in_3), .Q(out_5), .preset(button_5_out), .en(1'b1), .reset(button_6_out));  // open: Qn
  Button button_6 (.out(button_6_out));
endmodule
