// Logisim project Part2.circ as structural Verilog: 1 circuit, main circuit main
module main (
);

  wire button_1_out, button_2_out, button_3_out, button_4_out, button_5_out, button_6_out, button_7_out,
       button_8_out, button_9_out, button_10_out, j_k_ff_1_qn, j_k_ff_2_qn, not_1_out;
  wire [1:0] j_k_ff_1_q, j_k_ff_2_q;

  Button button_1 (.out(button_1_out));
  Button button_2 (.out(button_2_out));
  J_K_Flip_Flop j_k_ff_1 (
    .J(1'b1), .clk(button_1_out), .K(1'b1), .Q(j_k_ff_1_q[0]), .Qn(j_k_ff_1_qn), .preset(button_3_out),
    .en(1'b1), .reset(button_4_out));
  Button button_3 (.out(button_3_out));
  Button button_4 (.out(button_4_out));
  J_K_Flip_Flop j_k_ff_2 (
    .J(1'b1), .clk(button_2_out), .K(1'b1), .Q(j_k_ff_2_q[0]), .Qn(j_k_ff_2_qn), .preset(button_6_out),
    .en(1'b1), .reset(button_5_out));
  Button button_5 (.out(button_5_out));
  Button button_6 (.out(button_6_out));
  Button button_7 (.out(button_7_out));
  not not_1 (not_1_out, j_k_ff_2_qn);
  Button button_8 (.out(button_8_out));
  J_K_Flip_Flop j_k_ff_3 (
    .J(1'b1), .clk(j_k_ff_1_qn), .K(1'b1), .Q(j_k_ff_1_q[1]), .preset(button_7_out), .en(1'b1),
    .reset(button_9_out));  // open: Qn
  Button button_9 (.out(button_9_out));
  J_K_Flip_Flop j_k_ff_4 (
    .J(1'b1), .clk(not_1_out), .K(1'b1), .Q(j_k_ff_2_q[1]), .preset(button_8_out), .en(1'b1),
    .reset(button_10_out));  // open: Qn
  Button button_10 (.out(button_10_out));
  Hex_Digit_Display hex_digit_display_1 (.value({2'b00, j_k_ff_1_q}));  // open: dp
  Hex_Digit_Display hex_digit_display_2 (.value({2'b00, j_k_ff_2_q}));  // open: dp
endmodule
