// Logisim project Part2a.circ as structural Verilog: 1 circuit, main circuit main
module main (
  input  in_1,
  input  in_2
);

  wire button_2_out, button_3_out, button_4_out, button_5_out, clock_1_out, j_k_ff_1_qn, not_1_out;
  wire [1:0] j_k_ff_1_q;

  Button button_1 ();  // open: out
  Clock clock_1 (.out(clock_1_out));
  not not_1 (not_1_out, clock_1_out);
  Button button_2 (.out(button_2_out));
  J_K_Flip_Flop j_k_ff_1 (
    .J(1'b1), .clk(not_1_out), .K(1'b1), .Q(j_k_ff_1_q[0]), .Qn(j_k_ff_1_qn), .preset(button_2_out),
    .en(1'b1), .reset(button_3_out));
  Button button_3 (.out(button_3_out));
  J_K_Flip_Flop j_k_ff_2 (
    .J(1'b1), .clk(j_k_ff_1_qn), .K(1'b1), .Q(j_k_ff_1_q[1]), .preset(button_4_out), .en(1'b1),
    .reset(button_5_out));  // open: Qn
  Button button_4 (.out(button_4_out));
  Button button_5 (.out(button_5_out));
  Hex_Digit_Display hex_digit_display_1 (.value({in_2, in_1, j_k_ff_1_q}));  // open: dp
endmodule
