// Logisim project Part3.circ as structural Verilog: 3 circuits, main circuit main
module main (
);

  wire and_1_out, button_1_out, clock_1_out;
  wire [3:0] c1_1_out_3, c2_1_out_3, xnor_1_out;

  Clock clock_1 (.out(clock_1_out));
  Button button_1 (.out(button_1_out));
  Hex_Digit_Display hex_digit_display_1 (.value(c1_1_out_3));  // open: dp
  C1 c1_1 (.in_1(clock_1_out), .in_2(button_1_out), .out_3(c1_1_out_3));
  C2 c2_1 (.Reloj(clock_1_out), .in_2(button_1_out), .out_3(c2_1_out_3));
  Hex_Digit_Display hex_digit_display_2 (.value(c2_1_out_3));  // open: dp
  assign xnor_1_out = ~(c1_1_out_3 ^ c2_1_out_3);  // XNOR_Gate xnor_1, 4 bits wide
  and and_1 (and_1_out, xnor_1_out[0], xnor_1_out[1], xnor_1_out[2], xnor_1_out[3]);
  LED led_1 (.in(and_1_out));
endmodule

module C1 (
  input  in_1,
  input  in_2,
  output [3:0] out_3
);

  wire button_1_out, button_2_out, j_k_ff_1_qn;

  Button button_1 (.out(button_1_out));
  J_K_Flip_Flop j_k_ff_1 (
    .J(1'b1), .clk(in_1), .K(1'b1), .Q(out_3[0]), .Qn(j_k_ff_1_qn), .preset(button_1_out), .en(1'b1),
    .reset(in_2));
  J_K_Flip_Flop j_k_ff_2 (
    .J(1'b1), .clk(j_k_ff_1_qn), .K(1'b1), .Q(out_3[1]), .preset(button_2_out), .en(1'b1), .reset(in_2));  // open: Qn
  Button button_2 (.out(button_2_out));

  assign out_3[3:2] = 2'b00;
endmodule

module C2 (
  input  Reloj,
  input  in_2,
  output [3:0] out_3
);

  wire button_1_out, button_2_out;

  Button button_1 (.out(button_1_out));
  J_K_Flip_Flop j_k_ff_1 (
    .J(1'b1), .clk(Reloj), .K(1'b1), .Q(out_3[0]), .preset(button_1_out), .en(1'b1), .reset(in_2));  // open: Qn
  J_K_Flip_Flop j_k_ff_2 (
    .J(1'b1), .clk(out_3[0]), .K(1'b1), .Q(out_3[1]), .preset(in_2), .en(1'b1), .reset(button_2_out));  // open: Qn
  Button button_2 (.out(button_2_out));

  assign out_3[3:2] = 2'b00;
endmodule
