// Logisim project compare.circ as structural Verilog: 3 circuits, main circuit main
module main (
  output F
);

  wire button_1_out, button_2_out, button_3_out, button_4_out, clock_1_out, xnor_1_out, xnor_2_out;
  wire [3:0] c1_1_out_6, c2_1_out_6;

  Clock clock_1 (.out(clock_1_out));
  Button button_1 (.out(button_1_out));
  Button button_2 (.out(button_2_out));
  Button button_3 (.out(button_3_out));
  Button button_4 (.out(button_4_out));
  Hex_Digit_Display hex_digit_display_1 (.value(c1_1_out_6));  // open: dp
  C1 c1_1 (
    .Clock_Signal(clock_1_out), .Preset(button_1_out), .Preset_2(button_2_out), .out_6(c1_1_out_6),
    .Clear(button_1_out), .Clear_2(button_2_out));
  C2 c2_1 (
    .in_1(clock_1_out), .in_2(button_3_out), .in_4(button_4_out), .out_6(c2_1_out_6), .in_3(button_3_out),
    .in_5(button_4_out));
  Hex_Digit_Display hex_digit_display_2 (.value(c2_1_out_6));  // open: dp
  xnor xnor_1 (xnor_1_out, c1_1_out_6[0], c2_1_out_6[0]);
  xnor xnor_2 (xnor_2_out, c1_1_out_6[1], c2_1_out_6[1]);
  and and_1 (F, xnor_1_out, xnor_2_out);
endmodule

module C1 (
  input  Clock_Signal,
  input  Preset,
  input  Clear,
  input  Preset_2,
  input  Clear_2,
  output [3:0] out_6
);

  wire j_k_ff_1_qn;

  J_K_Flip_Flop j_k_ff_1 (
    .J(1'b1), .clk(Clock_Signal), .K(1'b1), .Q(out_6[0]), .Qn(j_k_ff_1_qn), .preset(Preset), .en(1'b1),
    .reset(Clear));
  J_K_Flip_Flop j_k_ff_2 (
    .J(1'b1), .clk(j_k_ff_1_qn), .K(1'b1), .Q(out_6[1]), .preset(Preset_2), .en(1'b1), .reset(Clear_2));  // open: Qn

  assign out_6[3:2] = 2'b00;
endmodule

module C2 (
  input  in_1,
  input  in_2,
  input  in_3,
  input  in_4,
  input  in_5,
  output [3:0] out_6
);

  wire j_k_ff_1_qn, not_1_out;

  J_K_Flip_Flop j_k_ff_1 (
    .J(1'b1), .clk(in_1), .K(1'b1), .Q(out_6[0]), .Qn(j_k_ff_1_qn), .preset(in_2), .en(1'b1), .reset(in_3));
  not not_1 (not_1_out, j_k_ff_1_qn);
  J_K_Flip_Flop j_k_ff_2 (
    .J(1'b1), .clk(not_1_out), .K(1'b1), .Q(out_6[1]), .preset(in_4), .en(1'b1), .reset(in_5));  // open: Qn

  assign out_6[3:2] = 2'b00;
endmodule
