// Logisim project Session5.circ as structural Verilog: 3 circuits, main circuit main
module main (
  input  E,
  input  Q2,
  input  Q1,
  input  Q0
);

  wire Clock_out, t2_1_f;

  Clock Clock (.out(Clock_out));
  T2 t2_1 (.E(E), .Q2(Q2), .Q1(Q1), .Q0(Q0), .F(t2_1_f));
  T_Flip_Flop t_ff_1 (.clk(Clock_out), .T(t2_1_f));  // open: Q, Qn, preset, reset, en
  D_Flip_Flop d_ff_1 ();  // open: clk, D, Q, Qn, preset, en, reset
  JK jk_1 ();  // open: in_1, out_2
  J_K_Flip_Flop j_k_ff_1 ();  // open: J, clk, K, Q, Qn, preset, en, reset
endmodule

module T2 (
  input  E,
  input  Q2,
  input  Q1,
  input  Q0,
  output F
);

  wire and_1_out, and_2_out, and_3_out, not_1_out, not_2_out, not_3_out;

  not not_1 (not_1_out, E);
  and and_1 (and_1_out, not_1_out, not_2_out, not_3_out);
  not not_2 (not_2_out, Q1);
  not not_3 (not_3_out, Q0);
  and and_2 (and_2_out, Q1, Q0);
  and and_3 (and_3_out, E, Q0);
  or or_1 (F, and_1_out, and_2_out, Q2, and_3_out);
endmodule

module JK (
  input  [3:0] in_1,
  output out_2
);

  wire decoder_1_out0, decoder_1_out1, decoder_1_out2, decoder_1_out3, decoder_1_out8, decoder_1_out9,
       decoder_1_out12, decoder_1_out13, or_1_out, or_2_out;

  Decoder #(.select(4)) decoder_1 (
    .out0(decoder_1_out0), .out1(decoder_1_out1), .out2(decoder_1_out2), .out3(decoder_1_out3),
    .out8(decoder_1_out8), .out9(decoder_1_out9), .out12(decoder_1_out12), .out13(decoder_1_out13),
    .sel(in_1), .en(1'b1));  // open: out4, out5, out6, out7, out10, out11, out14, out15
  or or_1 (or_1_out, decoder_1_out0, decoder_1_out1, decoder_1_out2, decoder_1_out3);
  or or_2 (or_2_out, decoder_1_out8, decoder_1_out9, decoder_1_out12, decoder_1_out13);
  or or_3 (out_2, or_1_out, or_2_out);
endmodule
