// Logisim project Session5Casa.circ as structural Verilog: 1 circuit, main circuit main
module main (
  input  E,
  output Q2,
  output Q1,
  output Q0,
  output S
);

  wire and_1_out, and_2_out, and_3_out, clock_1_out, d_ff_1_qn, decoder_1_out0, decoder_1_out1,
       decoder_1_out2, decoder_1_out3, decoder_1_out8, decoder_1_out9, decoder_1_out12, decoder_1_out13,
       j_k_ff_1_qn, not_1_out, or_1_out, or_2_out, or_3_out, or_4_out, Reset_out;

  Clock clock_1 (.out(clock_1_out));
  Button Reset (.out(Reset_out));
  not not_1 (not_1_out, E);
  Hex_Digit_Display hex_digit_display_1 (.value({1'b0, Q2, Q1, Q0}));  // open: dp
  and and_1 (and_1_out, Q1, Q0);
  and and_2 (and_2_out, Q0, E);
  and and_3 (and_3_out, not_1_out, j_k_ff_1_qn, d_ff_1_qn);
  T_Flip_Flop t_ff_1 (.clk(clock_1_out), .T(or_1_out), .Q(Q2), .reset(Reset_out));  // open: Qn, preset, en
  or or_1 (or_1_out, Q2, and_1_out, and_2_out, and_3_out);
  D_Flip_Flop d_ff_1 (.clk(clock_1_out), .D(Q2), .Q(Q1), .Qn(d_ff_1_qn), .reset(Reset_out));  // open: preset, en
  Decoder #(.select(4)) decoder_1 (
    .out0(decoder_1_out0), .out1(decoder_1_out1), .out2(decoder_1_out2), .out3(decoder_1_out3),
    .out8(decoder_1_out8), .out9(decoder_1_out9), .out12(decoder_1_out12), .out13(decoder_1_out13),
    .sel({E, Q2, Q1, Q0}), .en(1'b1));  // open: out4, out5, out6, out7, out10, out11, out14, out15
  or or_2 (or_2_out, Q0, Q1);
  or or_3 (or_3_out, decoder_1_out0, decoder_1_out2, decoder_1_out8, decoder_1_out12);
  or or_4 (or_4_out, decoder_1_out1, decoder_1_out3, decoder_1_out9, decoder_1_out13);
  J_K_Flip_Flop j_k_ff_1 (
    .J(or_3_out), .clk(clock_1_out), .K(or_4_out), .Q(Q0), .Qn(j_k_ff_1_qn), .reset(Reset_out));  // open: preset, en
  Multiplexer #(.select(2)) multiplexer_1 (
    .in0(d_ff_1_qn), .in1(1'b0), .in2(or_2_out), .in3(j_k_ff_1_qn), .out(S), .sel({E, Q1}), .en(1'b1));
endmodule
