// Logisim project Session 6.circ as structural Verilog: 1 circuit, main circuit main
module main (
  input  E0,
  input  E1,
  input  E2,
  input  m1,
  input  m0,
  output Output
);

  wire C_out, Clock_out, multiplexer_1_out, multiplexer_2_out, multiplexer_3_out, P_out;
  wire [2:1] d_ff_2_q;

  Clock Clock (.out(Clock_out));
  Button P (.out(P_out));
  Button C (.out(C_out));
  Multiplexer #(.select(2), .enable("false")) multiplexer_1 (
    .in0(1'b0), .in1(E2), .in2(d_ff_2_q[2]), .in3(d_ff_2_q[1]), .out(multiplexer_1_out), .sel({m1, m0}));
  D_Flip_Flop d_ff_1 (
    .clk(Clock_out), .D(multiplexer_1_out), .Q(d_ff_2_q[2]), .preset(P_out), .reset(C_out));  // open: Qn, en
  Multiplexer #(.select(2), .enable("false")) multiplexer_2 (
    .in0(d_ff_2_q[2]), .in1(E1), .in2(d_ff_2_q[1]), .out(multiplexer_2_out), .sel({m1, m0}));  // open: in3
  Multiplexer #(.select(2), .enable("false")) multiplexer_3 (
    .in0(d_ff_2_q[1]), .in1(E0), .in2(Output), .in3(1'b0), .out(multiplexer_3_out), .sel({m1, m0}));
  D_Flip_Flop d_ff_2 (
    .clk(Clock_out), .D(multiplexer_2_out), .Q(d_ff_2_q[1]), .preset(P_out), .reset(C_out));  // open: Qn, en
  D_Flip_Flop d_ff_3 (
    .clk(Clock_out), .D(multiplexer_3_out), .Q(Output), .preset(P_out), .reset(C_out));  // open: Qn, en
  Hex_Digit_Display hex_digit_display_1 (.value({1'b0, d_ff_2_q, Output}));  // open: dp
endmodule
